# Fritzing sketch 16x9_G_Click (saved by Fritzing 0.9.3b)

parts:
  Composant1 = Mikrobus Prototype Board
  Composant2 = Arduino Uno (Rev3) - ICSP

nets:
  N1: Composant1.CS1, Composant2.D10_PWM/SS
  GND1: Composant1.GND1, Composant2.GND
  N2: Composant1.SCL3, Composant1.SCL4, Composant2.A5/SCL
  N3: Composant1.SDA2, Composant1.SDA4, Composant2.A4/SDA
  N4: Composant1.+5V2, Composant1.+5V4, Composant2.5V

custom parts:
  Mikrobus Prototype Board: Mikrobus Prototype board
