# Fritzing sketch 4x4_RGB_Click (saved by Fritzing 0.9.3b)

parts:
  Composant1 = Mikrobus Prototype Board
  Composant2 = Arduino Uno (Rev3) - ICSP

nets:
  N1: Composant1.RST1, Composant2.A3
  GND1: Composant1.GND1, Composant1.GND4, Composant2.GND
  N2: Composant1.+5V4, Composant2.5V

custom parts:
  Mikrobus Prototype Board: Mikrobus Prototype board
