# Fritzing sketch Bargraph_Click (saved by Fritzing 0.9.3b)

parts:
  Composant1 = Mikrobus Prototype Board
  Composant2 = Arduino Uno (Rev3) - ICSP

nets:
  N1: Composant1.CS1, Composant2.D10_PWM/SS
  N2: Composant1.SCK1, Composant2.D13/SCK
  N3: Composant1.MOSI1, Composant1.MOSI4, Composant2.D11_PWM/MOSI
  GND1: Composant1.GND1, Composant1.GND8, Composant2.GND
  N4: Composant1.PWM4, Composant2.D6_PWM
  N5: Composant1.+5V4, Composant2.5V

custom parts:
  Mikrobus Prototype Board: Mikrobus Prototype board
