# Fritzing sketch Relay_2_Click (saved by Fritzing 0.9.3b)
breadboards: 1

parts:
  Composant1 = Mikrobus Prototype Board
  Composant2 = Arduino Uno (Rev3) - ICSP
  R1 = Resistor [tolerance=±5% resistance=1k package=THT]
  R2 = Resistor [tolerance=±5% resistance=1k package=THT]
  R3 = Resistor [tolerance=±5% resistance=2.2k package=THT]
  R4 = Resistor [tolerance=±5% resistance=2.2k package=THT]

nets:
  N1: Composant1.AN1, R2.Pin_1, R4.Pin_0
  N2: Composant1.+3.3v-1, Composant2.3V3
  GND1: Composant1.GND1, Composant2.GND, R3.Pin_1, R4.Pin_1
  N3: Composant1.PWM4, R1.Pin_1, R3.Pin_0
  N4: Composant2.A0, R2.Pin_0
  N5: Composant2.D6_PWM, R1.Pin_0

custom parts:
  Mikrobus Prototype Board: Mikrobus Prototype board
