# Fritzing sketch Stepper_Click (saved by Fritzing 0.9.3b)

parts:
  Composant1 = Mikrobus Prototype Board
  Composant2 = Arduino Uno (Rev3) - ICSP
  S1 = Pushbutton [package=THT]

nets:
  N1: Composant1.AN1, Composant2.A0
  N2: Composant1.RST1, Composant2.A3
  N3: Composant1.CS1, Composant2.D10_PWM/SS
  GND1: Composant1.GND1, Composant1.GND2, Composant2.GND, S1.leg1
  N4: Composant1.PWM4, Composant2.D6_PWM
  N5: Composant1.+5V3, Composant1.+5V4, Composant2.5V
  N6: Composant2.D5_PWM, S1.leg0

custom parts:
  Mikrobus Prototype Board: Mikrobus Prototype board
