# Fritzing sketch Touchpad_Click (saved by Fritzing 0.9.3b)
breadboards: 1

parts:
  Composant1 = Mikrobus Prototype Board
  Composant2 = Arduino Uno (Rev3) - ICSP
  Composant3 = TXB0108 8-channel Bi-directional Logic Level Converter  # not connected

nets:
  N1: Composant1.+3.3v-1, Composant2.3V3
  GND1: Composant1.GND1, Composant2.GND

custom parts:
  Mikrobus Prototype Board: Mikrobus Prototype board
  TXB0108 8-channel Bi-directional Logic Level Converter: Because the Arduino (and Basic Stamp) are 5V devices, and most modern sensors, displays, flash cards and modes are 3.3V-only, many makers find that they need to perform level shifting/conversion to protect the 3.3V device from 5V. Although one can use resistors to make a divider, for high speed transfers, the resistors can add a lot of slew and cause havoc that is tough to debug. For that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
