# Fritzing sketch Vibra_sense_Click (saved by Fritzing 0.9.3b)

parts:
  Composant1 = Mikrobus Prototype Board
  Composant2 = Arduino Uno (Rev3) - ICSP
  Composant3 = Mikrobus Prototype Board

nets:
  N1: Composant1.RST1, Composant2.A2
  GND1: Composant1.GND1, Composant2.GND, Composant3.GND1, Composant3.GND7
  N2: Composant1.+5V4, Composant2.5V, Composant3.+5V4
  N3: Composant2.A3, Composant3.RST1
  N4: Composant2.D2, Composant3.INT4

custom parts:
  Mikrobus Prototype Board: Mikrobus Prototype board
